// Logisim project D_flip.circ as structural Verilog: 1 circuit, main circuit main
module main (
  input  R,
  input  in_2,
  output NOT_Q
);

  wire and_1_out, button_1_out, d_latch_1_q, d_latch_2_q, not_1_out, not_2_out, not_3_out, or_1_out;

  not not_1 (not_1_out, d_latch_2_q);
  Button button_1 (.out(button_1_out));
  not not_2 (not_2_out, button_1_out);
  or or_1 (or_1_out, R, button_1_out);
  not not_3 (not_3_out, R);
  D_latch d_latch_1 (.D(not_1_out), .WE(not_2_out), .Q(d_latch_1_q));  // open: NOT_Q
  and and_1 (and_1_out, not_3_out, d_latch_1_q);
  D_latch d_latch_2 (.D(and_1_out), .WE(or_1_out), .Q(d_latch_2_q), .NOT_Q(NOT_Q));
endmodule
