// Logisim project D_latch.circ as structural Verilog: 1 circuit, main circuit D_latch
module D_latch (
  input  D,
  input  WE,
  output Q,
  output NOT_Q
);

  wire and_1_out, and_2_out, not_1_out;

  not not_1 (not_1_out, D);
  and and_1 (and_1_out, not_1_out, WE);
  and and_2 (and_2_out, WE, D);
  nor nor_1 (Q, and_1_out, NOT_Q);
  nor nor_2 (NOT_Q, Q, and_2_out);

  // Notes on the sheet:
  //   Q
  //   ~Q
endmodule
