// Logisim project Decoder_4To16_fixed.circ as structural Verilog: 1 circuit, main circuit main
module main (
  input  A0,
  input  A1,
  input  A2,
  input  A3,
  input  EN,
  output D0,
  output D1,
  output D2,
  output D3,
  output D4,
  output D5,
  output D6,
  output D7,
  output D8,
  output D9,
  output D10,
  output D11,
  output D12,
  output D13,
  output D14,
  output D15
);

  wire and_1_out, and_2_out, not_1_out;

  not not_1 (not_1_out, A0);
  and and_1 (and_1_out, not_1_out, EN);
  and and_2 (and_2_out, EN, A0);
  Decoder_3To8 decoder_3to8_1 (
    .A0(A3), .A1(A2), .A2(A1), .EN(and_1_out), .D0(D0), .D1(D2), .D2(D4), .D3(D6), .D4(D8), .D5(D10),
    .D6(D12), .D7(D14));
  Decoder_3To8 decoder_3to8_2 (
    .A0(A3), .A1(A2), .A2(A1), .EN(and_2_out), .D0(D1), .D1(D3), .D2(D5), .D3(D7), .D4(D9), .D5(D11),
    .D6(D13), .D7(D15));
endmodule
