// Logisim project Encoder.circ as structural Verilog: 3 circuits, main circuit main
module Encoder_4To2 (
  input  A0,
  input  A1,
  input  A2,
  input  A3,
  output Y0,
  output Y1
);

  or or_1 (Y0, A1, A3);
  or or_2 (Y1, A3, A2);
endmodule

module Encoder_16To4 (
  input  A0,
  input  A1,
  input  A2,
  input  A3,
  input  A4,
  input  A5,
  input  A6,
  input  A7,
  input  A8,
  input  A9,
  input  A10,
  input  A11,
  input  A12,
  input  A13,
  input  A14,
  input  A15,
  output Y0,
  output Y1,
  output Y2,
  output Y3
);

  or or_1 (Y3, A8, A9, A10, A11, A12, A13, A14, A15);
  or or_2 (Y2, A12, A13, A4, A5, A6, A7, A14, A15);
  or or_3 (Y1, A2, A3, A6, A7, A10, A11, A14, A15);
  or or_4 (Y0, A1, A3, A5, A7, A9, A11, A13, A15);
endmodule

module main (
  input  in_1
);

  wire dipswitch_1_p1, dipswitch_1_p2, dipswitch_1_p3, dipswitch_1_p4, dipswitch_1_p5, dipswitch_1_p6,
       dipswitch_1_p7, dipswitch_1_p8, dipswitch_1_p9, dipswitch_1_p10, dipswitch_1_p11, dipswitch_1_p12,
       dipswitch_1_p13, dipswitch_1_p14, dipswitch_1_p15, dipswitch_1_p16, encoder_16to4_1_y0,
       encoder_16to4_1_y1, encoder_16to4_1_y2, encoder_16to4_1_y3;

  // DipSwitch #(.number(16)) dipswitch_1: pin names not known; wires that end beside it: dipswitch_1_p1, dipswitch_1_p2, dipswitch_1_p3, dipswitch_1_p4, dipswitch_1_p5, dipswitch_1_p6, dipswitch_1_p7, dipswitch_1_p8, dipswitch_1_p9, dipswitch_1_p10, dipswitch_1_p11, dipswitch_1_p12, dipswitch_1_p13, dipswitch_1_p14, dipswitch_1_p15, dipswitch_1_p16
  Encoder_16To4 encoder_16to4_1 (
    .A0(dipswitch_1_p1), .A1(dipswitch_1_p2), .A2(dipswitch_1_p3), .A3(dipswitch_1_p4), .A4(dipswitch_1_p5),
    .A5(dipswitch_1_p6), .A6(dipswitch_1_p7), .A7(dipswitch_1_p8), .A8(dipswitch_1_p9), .A9(dipswitch_1_p10),
    .A10(dipswitch_1_p11), .A11(dipswitch_1_p12), .A12(dipswitch_1_p13), .A13(dipswitch_1_p14),
    .A14(dipswitch_1_p15), .A15(dipswitch_1_p16), .Y0(encoder_16to4_1_y0), .Y1(encoder_16to4_1_y1),
    .Y2(encoder_16to4_1_y2), .Y3(encoder_16to4_1_y3));
  Seven_segment16 seven_segment16_1 (
    .in_1(in_1), .in_2(encoder_16to4_1_y0), .in_3(encoder_16to4_1_y1), .in_4(encoder_16to4_1_y2),
    .in_5(encoder_16to4_1_y3));
endmodule
