// Logisim project F6.circ as structural Verilog: 11 circuits, main circuit main
module GPR (
  input  clk,
  input  [31:0] wdata,
  input  [3:0] waddr,
  input  wen,
  input  [3:0] raddr1,
  input  [3:0] raddr2,
  input  reset,
  output [31:0] rdata1,
  output [31:0] rdata2
);

  wire decoder_1_out0, decoder_1_out1, decoder_1_out2, decoder_1_out3, decoder_1_out4, decoder_1_out5,
       decoder_1_out6, decoder_1_out7, decoder_1_out8, decoder_1_out9, decoder_1_out10, decoder_1_out11,
       decoder_1_out12, decoder_1_out13, decoder_1_out14, decoder_1_out15;
  wire [31:0] register_1_q, register_2_q, register_3_q, register_4_q, register_5_q, register_6_q,
       register_7_q, register_8_q, register_9_q, register_10_q, register_11_q, register_12_q, register_13_q,
       register_14_q, register_15_q, register_16_q;

  Decoder #(.select(4)) decoder_1 (
    .out0(decoder_1_out0), .out1(decoder_1_out1), .out2(decoder_1_out2), .out3(decoder_1_out3),
    .out4(decoder_1_out4), .out5(decoder_1_out5), .out6(decoder_1_out6), .out7(decoder_1_out7),
    .out8(decoder_1_out8), .out9(decoder_1_out9), .out10(decoder_1_out10), .out11(decoder_1_out11),
    .out12(decoder_1_out12), .out13(decoder_1_out13), .out14(decoder_1_out14), .out15(decoder_1_out15),
    .sel(waddr), .en(wen));
  Register #(.width(32)) register_1 (.D(wdata), .en(decoder_1_out0), .clk(clk), .Q(register_1_q), .clr(1'b1));
  Register #(.width(32)) register_2 (.D(wdata), .en(decoder_1_out8), .clk(clk), .Q(register_2_q), .clr(reset));
  Register #(.width(32)) register_3 (.D(wdata), .en(decoder_1_out1), .clk(clk), .Q(register_3_q), .clr(reset));
  Register #(.width(32)) register_4 (.D(wdata), .en(decoder_1_out9), .clk(clk), .Q(register_4_q), .clr(reset));
  Register #(.width(32)) register_5 (.D(wdata), .en(decoder_1_out2), .clk(clk), .Q(register_5_q), .clr(reset));
  Register #(.width(32)) register_6 (.D(wdata), .en(decoder_1_out10), .clk(clk), .Q(register_6_q), .clr(reset));
  Register #(.width(32)) register_7 (.D(wdata), .en(decoder_1_out3), .clk(clk), .Q(register_7_q), .clr(reset));
  Register #(.width(32)) register_8 (.D(wdata), .en(decoder_1_out11), .clk(clk), .Q(register_8_q), .clr(reset));
  Register #(.width(32)) register_9 (.D(wdata), .en(decoder_1_out4), .clk(clk), .Q(register_9_q), .clr(reset));
  Register #(.width(32)) register_10 (.D(wdata), .en(decoder_1_out12), .clk(clk), .Q(register_10_q), .clr(reset));
  Register #(.width(32)) register_11 (.D(wdata), .en(decoder_1_out5), .clk(clk), .Q(register_11_q), .clr(reset));
  Register #(.width(32)) register_12 (.D(wdata), .en(decoder_1_out13), .clk(clk), .Q(register_12_q), .clr(reset));
  Register #(.width(32)) register_13 (.D(wdata), .en(decoder_1_out6), .clk(clk), .Q(register_13_q), .clr(reset));
  Register #(.width(32)) register_14 (.D(wdata), .en(decoder_1_out14), .clk(clk), .Q(register_14_q), .clr(reset));
  Register #(.width(32)) register_15 (.D(wdata), .en(decoder_1_out7), .clk(clk), .Q(register_15_q), .clr(reset));
  Register #(.width(32)) register_16 (.D(wdata), .en(decoder_1_out15), .clk(clk), .Q(register_16_q), .clr(reset));
  Multiplexer #(.select(4), .width(32)) multiplexer_1 (
    .in0(register_1_q), .in1(register_3_q), .in2(register_5_q), .in3(register_7_q), .in4(register_9_q),
    .in5(register_11_q), .in6(register_13_q), .in7(register_15_q), .in8(register_2_q), .in9(register_4_q),
    .in10(register_6_q), .in11(register_8_q), .in12(register_10_q), .in13(register_12_q),
    .in14(register_14_q), .in15(register_16_q), .out(rdata1), .sel(raddr1));
  Multiplexer #(.select(4), .width(32)) multiplexer_2 (
    .in0(register_1_q), .in1(register_3_q), .in2(register_5_q), .in3(register_7_q), .in4(register_9_q),
    .in5(register_11_q), .in6(register_13_q), .in7(register_15_q), .in8(register_2_q), .in9(register_4_q),
    .in10(register_6_q), .in11(register_8_q), .in12(register_10_q), .in13(register_12_q),
    .in14(register_14_q), .in15(register_16_q), .out(rdata2), .sel(raddr2));
endmodule

module main (
  input  reset,
  input  in_2,
  input  in_3
);

  wire add, addi, and_1_out, and_2_out, and_3_out, and_11_out, CLK, clock_3_out, comparator_1_eq,
       comparator_2_eq, comparator_4_eq, comparator_5_eq, comparator_6_eq, comparator_7_eq, comparator_8_eq,
       comparator_9_eq, comparator_10_eq, comparator_11_eq, comparator_12_eq, comparator_13_eq,
       comparator_14_eq, comparator_15_gt, comparator_16_lt, comparator_17_eq, comparator_18_eq,
       decoder_1_out0, decoder_1_out1, decoder_1_out2, decoder_1_out3, decoder_1_out4, decoder_1_out5,
       decoder_1_out6, decoder_1_out7, decoder_1_out8, decoder_1_out9, decoder_1_out10, decoder_1_out11,
       decoder_1_out12, decoder_1_out13, decoder_1_out14, decoder_1_out15, decoder_2_out0, decoder_2_out1,
       decoder_2_out2, decoder_2_out3, GPR_wen, isRAM, isVGA, jalr, lbu, lui, lw, or_5_out, or_6_out,
       or_7_out, or_8_out, RAM_WE, sb, store_byte_1_ram_we, store_word_1_ram_we, sw;
  wire [1:0] Byte_addr;
  wire [2:0] funct_12_14;
  wire [4:0] imm_4_0, imm_11_0;
  wire [6:0] funct7, opcode_6_0;
  wire [7:0] Byte0, Byte1, Byte2, Byte3, multiplexer_1_out, store_byte_1_ram_data_in,
       store_byte_1_ram_data_in_2, store_byte_1_ram_data_in_3, store_byte_1_ram_data_in_4, X, Y;
  wire [7:3] imm_31_12;
  wire [31:0] add_result, adder_1_out, addi_result, GPR_wdata, imm_lui, jalr_target_addr, lbu_out,
       load_byte_unsigned_1_ram_byte_addr_32, load_word_1_ram_byte_addr_32, lw_out, multiplexer_2_out,
       or_4_out, pc_1_pc_out_data, rdata1, rdata2, register_1_q, register_2_q, register_3_q, register_4_q,
       register_5_q, register_6_q, register_7_q, register_8_q, register_9_q, register_10_q, register_11_q,
       register_12_q, register_13_q, register_14_q, register_15_q, register_16_q,
       store_byte_1_ram_byte_addr_32, store_word_1_ram_byte_addr_32, store_word_1_ram_data_in;
  wire [31:18] or_3_out;

  // Probe on jalr_target_addr
  Multiplexer #(.select(2), .width(8)) multiplexer_1 (
    .in0(Byte0), .in1(Byte1), .in2(Byte2), .in3(Byte3), .out(multiplexer_1_out), .sel(Byte_addr));
  // Probe on lw_out
  PC pc_1 (
    .PC_load_data(jalr_target_addr), .PC_load_en(jalr), .clk(CLK), .PC_reset(in_2),
    .PC_out_data(pc_1_pc_out_data));
  // Probe on GPR_wdata
  Clock clock_1 ();  // open: out
  // Probe on imm_lui
  assign GPR_wdata = multiplexer_2_out | addi_result | imm_lui | lw_out | add_result | lbu_out;  // OR_Gate or_1, 32 bits wide
  load_byte_unsigned load_byte_unsigned_1 (
    .imm_11_0({funct7, imm_11_0}), .rdata1(rdata1), .lbu_EN(lbu), .RAM_data_out(multiplexer_1_out),
    .RAM_byte_addr_32(load_byte_unsigned_1_ram_byte_addr_32), .GPR_wdata(lbu_out));  // open: RAM_OE
  store_byte store_byte_1 (
    .imm_4_0(imm_4_0), .imm_11_5(funct7), .rdata1(rdata1), .sb_EN(sb), .rdata2(rdata2),
    .RAM_byte_addr_32(store_byte_1_ram_byte_addr_32), .RAM_WE(store_byte_1_ram_we),
    .RAM_data_in({store_byte_1_ram_data_in_3, store_byte_1_ram_data_in_2, store_byte_1_ram_data_in, store_byte_1_ram_data_in_4}));
  Adder #(.width(32)) adder_1 (.a(pc_1_pc_out_data), .b(32'h4), .out(adder_1_out));  // open: cin, cout
  // Probe on lbu_out
  // Probe on lw_out
  Decoder #(.select(4)) decoder_1 (
    .out0(decoder_1_out0), .out1(decoder_1_out1), .out2(decoder_1_out2), .out3(decoder_1_out3),
    .out4(decoder_1_out4), .out5(decoder_1_out5), .out6(decoder_1_out6), .out7(decoder_1_out7),
    .out8(decoder_1_out8), .out9(decoder_1_out9), .out10(decoder_1_out10), .out11(decoder_1_out11),
    .out12(decoder_1_out12), .out13(decoder_1_out13), .out14(decoder_1_out14), .out15(decoder_1_out15),
    .sel(imm_4_0[3:0]), .en(GPR_wen));
  load_upper_immediate load_upper_immediate_1 (
    .imm_31_12({funct7, imm_11_0, imm_31_12, funct_12_14}), .lui_en(lui), .imm_lui(imm_lui));
  jump_and_link_register jump_and_link_register_1 (
    .rdata1(rdata1), .imm_11_0({funct7, imm_11_0}), .jalr(jalr), .jalr_target_addr(jalr_target_addr));
  add_immediate add_immediate_1 (
    .rdata1(rdata1), .imm_11_0({funct7, imm_11_0}), .addi_en(addi), .addi_result(addi_result));
  addd addd_1 (.rdata1(rdata1), .rdata2(rdata2), .addd_en(add), .add_result(add_result));
  load_word load_word_1 (
    .imm_11_0({funct7, imm_11_0}), .rdata1(rdata1), .lw_EN(lw), .RAM_data_out({Byte3, Byte2, Byte1, Byte0}),
    .RAM_byte_addr_32(load_word_1_ram_byte_addr_32), .GPR_wdata(lw_out));  // open: RAM_OE
  store_word store_word_1 (
    .imm_4_0(imm_4_0), .imm_11_5(funct7), .rdata1(rdata1), .sw_EN(sw), .rdata2(rdata2),
    .RAM_byte_addr_32(store_word_1_ram_byte_addr_32), .RAM_WE(store_word_1_ram_we),
    .RAM_data_in(store_word_1_ram_data_in));
  Multiplexer #(.width(32)) multiplexer_2 (.in0({32{1'b0}}), .in1(adder_1_out), .out(multiplexer_2_out), .sel(jalr));
  Register #(.width(32)) register_1 (.D(GPR_wdata), .en(decoder_1_out0), .clk(CLK), .Q(register_1_q), .clr(1'b1));
  Register #(.width(32)) register_2 (.D(GPR_wdata), .en(decoder_1_out8), .clk(CLK), .Q(register_2_q), .clr(reset));
  ROM #(.addrWidth(20), .dataWidth(32)) rom_1 (
    .addr(pc_1_pc_out_data[21:2]), .data({funct7, imm_11_0, imm_31_12, funct_12_14, imm_4_0, opcode_6_0}));
  and and_1 (and_1_out, store_byte_1_ram_we, isRAM);
  Register #(.width(32)) register_3 (.D(GPR_wdata), .en(decoder_1_out1), .clk(CLK), .Q(register_3_q), .clr(reset));
  Register #(.width(32)) register_4 (.D(GPR_wdata), .en(decoder_1_out9), .clk(CLK), .Q(register_4_q), .clr(reset));
  Clock clock_2 (.out(CLK));
  Register #(.width(32)) register_5 (.D(GPR_wdata), .en(decoder_1_out2), .clk(CLK), .Q(register_5_q), .clr(reset));
  Register #(.width(32)) register_6 (.D(GPR_wdata), .en(decoder_1_out10), .clk(CLK), .Q(register_6_q), .clr(reset));
  // Probe on jalr_target_addr
  // Probe on {or_3_out, Y, X, Byte_addr}
  // Probe on load_word_1_ram_byte_addr_32
  and and_2 (and_2_out, store_word_1_ram_we, isRAM);
  or or_2 (RAM_WE, and_2_out, and_1_out);
  Register #(.width(32)) register_7 (.D(GPR_wdata), .en(decoder_1_out3), .clk(CLK), .Q(register_7_q), .clr(reset));
  Register #(.width(32)) register_8 (.D(GPR_wdata), .en(decoder_1_out11), .clk(CLK), .Q(register_8_q), .clr(reset));
  Register #(.width(32)) register_9 (.D(GPR_wdata), .en(decoder_1_out4), .clk(CLK), .Q(register_9_q), .clr(reset));
  Register #(.width(32)) register_10 (.D(GPR_wdata), .en(decoder_1_out12), .clk(CLK), .Q(register_10_q), .clr(reset));
  assign {or_3_out, Y, X, Byte_addr} = load_word_1_ram_byte_addr_32 | store_word_1_ram_byte_addr_32 | load_byte_unsigned_1_ram_byte_addr_32 | store_byte_1_ram_byte_addr_32;  // OR_Gate or_3, 32 bits wide
  assign or_4_out = store_word_1_ram_data_in | {store_byte_1_ram_data_in_4, store_byte_1_ram_data_in_4, store_byte_1_ram_data_in_4, store_byte_1_ram_data_in_4};  // OR_Gate or_4, 32 bits wide
  Register #(.width(32)) register_11 (.D(GPR_wdata), .en(decoder_1_out5), .clk(CLK), .Q(register_11_q), .clr(reset));
  Register #(.width(32)) register_12 (.D(GPR_wdata), .en(decoder_1_out13), .clk(CLK), .Q(register_12_q), .clr(reset));
  // Probe on store_byte_1_ram_byte_addr_32
  Register #(.width(32)) register_13 (.D(GPR_wdata), .en(decoder_1_out6), .clk(CLK), .Q(register_13_q), .clr(reset));
  Register #(.width(32)) register_14 (.D(GPR_wdata), .en(decoder_1_out14), .clk(CLK), .Q(register_14_q), .clr(reset));
  // Probe on {or_3_out, Y, X, Byte_addr}
  // Probe on or_4_out
  and and_3 (and_3_out, sw, isRAM);
  Register #(.width(32)) register_15 (.D(GPR_wdata), .en(decoder_1_out7), .clk(CLK), .Q(register_15_q), .clr(reset));
  Register #(.width(32)) register_16 (.D(GPR_wdata), .en(decoder_1_out15), .clk(CLK), .Q(register_16_q), .clr(reset));
  Decoder #(.enable("false"), .select(2)) decoder_2 (
    .out0(decoder_2_out0), .out1(decoder_2_out1), .out2(decoder_2_out2), .out3(decoder_2_out3),
    .sel(Byte_addr));
  Comparator #(.mode("unsigned"), .width(7)) comparator_1 (
    .a(opcode_6_0), .b(7'b1100111), .eq(comparator_1_eq));  // open: gt, lt
  Comparator #(.mode("unsigned"), .width(3)) comparator_2 (
    .a(funct_12_14), .b(3'b000), .eq(comparator_2_eq));  // open: gt, lt
  Comparator #(.mode("unsigned"), .width(7)) comparator_3 (.a(opcode_6_0), .b(7'b0110111), .eq(lui));  // open: gt, lt
  Comparator #(.mode("unsigned"), .width(7)) comparator_4 (
    .a(opcode_6_0), .b(7'b0110011), .eq(comparator_4_eq));  // open: gt, lt
  Comparator #(.mode("unsigned"), .width(3)) comparator_5 (
    .a(funct_12_14), .b(3'b000), .eq(comparator_5_eq));  // open: gt, lt
  Comparator #(.mode("unsigned"), .width(7)) comparator_6 (
    .a(funct7), .b({7{1'b0}}), .eq(comparator_6_eq));  // open: gt, lt
  Comparator #(.mode("unsigned"), .width(7)) comparator_7 (
    .a(opcode_6_0), .b(7'b0000011), .eq(comparator_7_eq));  // open: gt, lt
  Comparator #(.mode("unsigned"), .width(3)) comparator_8 (
    .a(funct_12_14), .b(3'b010), .eq(comparator_8_eq));  // open: gt, lt
  Comparator #(.mode("unsigned"), .width(7)) comparator_9 (
    .a(opcode_6_0), .b(7'b0100011), .eq(comparator_9_eq));  // open: gt, lt
  Comparator #(.mode("unsigned"), .width(3)) comparator_10 (
    .a(funct_12_14), .b(3'b010), .eq(comparator_10_eq));  // open: gt, lt
  Comparator #(.mode("unsigned"), .width(7)) comparator_11 (
    .a(opcode_6_0), .b(7'b0000011), .eq(comparator_11_eq));  // open: gt, lt
  Comparator #(.mode("unsigned"), .width(3)) comparator_12 (
    .a(funct_12_14), .b(3'b100), .eq(comparator_12_eq));  // open: gt, lt
  Comparator #(.mode("unsigned"), .width(7)) comparator_13 (
    .a(opcode_6_0), .b(7'b0100011), .eq(comparator_13_eq));  // open: gt, lt
  Comparator #(.mode("unsigned"), .width(3)) comparator_14 (
    .a(funct_12_14), .b(3'b000), .eq(comparator_14_eq));  // open: gt, lt
  Comparator #(.mode("unsigned"), .width(32)) comparator_15 (
    .a({or_3_out, Y, X, Byte_addr}), .b(32'h20000000), .gt(comparator_15_gt));  // open: eq, lt
  Comparator #(.mode("unsigned"), .width(32)) comparator_16 (
    .a({or_3_out, Y, X, Byte_addr}), .b(32'h20040000), .lt(comparator_16_lt));  // open: gt, eq
  and and_4 (jalr, comparator_1_eq, comparator_2_eq);
  and and_5 (add, comparator_4_eq, comparator_6_eq, comparator_5_eq);
  and and_6 (lw, comparator_7_eq, comparator_8_eq);
  and and_7 (sw, comparator_9_eq, comparator_10_eq);
  and and_8 (lbu, comparator_11_eq, comparator_12_eq);
  and and_9 (sb, comparator_13_eq, comparator_14_eq);
  // Probe on {or_3_out[21:18], Y, X}
  or or_5 (or_5_out, and_3_out, decoder_2_out0);
  or or_6 (or_6_out, and_3_out, decoder_2_out1);
  or or_7 (or_7_out, and_3_out, decoder_2_out2);
  or or_8 (or_8_out, and_3_out, decoder_2_out3);
  Multiplexer #(.select(4), .width(32)) multiplexer_3 (
    .in0(register_1_q), .in1(register_3_q), .in2(register_5_q), .in3(register_7_q), .in4(register_9_q),
    .in5(register_11_q), .in6(register_13_q), .in7(register_15_q), .in8(register_2_q), .in9(register_4_q),
    .in10(register_6_q), .in11(register_8_q), .in12(register_10_q), .in13(register_12_q),
    .in14(register_14_q), .in15(register_16_q), .out(rdata1), .sel(imm_31_12[6:3]));
  Multiplexer #(.select(4), .width(32)) multiplexer_4 (
    .in0(register_1_q), .in1(register_3_q), .in2(register_5_q), .in3(register_7_q), .in4(register_9_q),
    .in5(register_11_q), .in6(register_13_q), .in7(register_15_q), .in8(register_2_q), .in9(register_4_q),
    .in10(register_6_q), .in11(register_8_q), .in12(register_10_q), .in13(register_12_q),
    .in14(register_14_q), .in15(register_16_q), .out(rdata2), .sel(imm_11_0[3:0]));
  Clock clock_3 (.out(clock_3_out));
  and and_10 (isVGA, comparator_15_gt, comparator_16_lt);
  RAM #(.addrWidth(20), .asyncread("true"), .byteenables("byteEnables"), .dataWidth(32), .\type ("nonvolatile")) ram_1 (
    .addr({or_3_out[21:18], Y, X}), .we(RAM_WE), .oe(1'b1), .clk(CLK), .din(or_4_out),
    .dout({Byte3, Byte2, Byte1, Byte0}), .be3(or_8_out), .be2(or_7_out), .be1(or_6_out), .be0(or_5_out));
  Comparator #(.mode("unsigned"), .width(7)) comparator_17 (
    .a(opcode_6_0), .b(7'b0010011), .eq(comparator_17_eq));  // open: gt, lt
  Comparator #(.mode("unsigned"), .width(3)) comparator_18 (
    .a(funct_12_14), .b(3'b000), .eq(comparator_18_eq));  // open: gt, lt
  not not_1 (isRAM, isVGA);
  and and_11 (and_11_out, sw, isVGA);
  and and_12 (addi, comparator_17_eq, comparator_18_eq);
  or or_9 (GPR_wen, lbu, addi, lw, lui, jalr, add);
  // RGB_Video #(.cursor("No Cursor"), .height(256), .width(256)) rgb_video_1: pin names not known; wires that end beside it: in_3, clock_3_out, and_11_out, X, Y, rdata2[23:0]

  // Other names for the same wires on the sheet: rd_4_0[3:0] = imm_4_0[3:0];
  //   imm_31_12 (some bits) = {funct7, imm_11_0, funct_12_14}; rs1[3:0] = imm_31_12[6:3]; rs2[3:0] = imm_11_0[3:0];
  //   imm_11_0[11:5] = funct7; imm_11_5[6:0] = funct7; Power_On_Reset = in_3;
  //   RAM_data_out[31:0] = {Byte3, Byte2, Byte1, Byte0}; RGB_Data_in[23:0] = rdata2[23:0]

  // Notes on the sheet:
  //   contents of rom_1 (hex, n*v repeats v):
  //   413 93137 10113 10b7 dbc08093 80e7 fe012823 fea10923 fea12423 fe914203 fe4109a3 ff012783 f787b3
  //   f787b3 4b6b7 af868693 fdc10113 d787b3 10000713 f12423 10593 100793 b00513 2112023 12023 12223 e12623
  //   e12823 f10a23 10b7 a8408093 80e7 2012083 2410113 8067 ff410113 112423 10b7 a7c08093 80e7 513 1800093
  //   80e7 812083 513 c10113 8067 852583 feb12823 fe812e23 3437 80840413 ff014183 3401b3 1c183 ff114203
  //   440233 24203 4181b3 ff214203 440233 24203 4181b3 ff314203 440233 24203 4181b3 3237 80020213 320233
  //   24203 ffc12403 420233 420233 410233 11b7 86418193 fe312823 14800193 fe312623 fec22203 20067 1052703
  //   52683 452783 fe810113 e12423 112a23 812823 912623 fed12823 fef12623 13737 a0070713 fe012223 ff314203
  //   fe4102a3 fef14203 fe410223 fe412203 470233 24203 fe4105a3 ff214203 fe4102a3 fee14203 fe410223
  //   fe412203 470233 24203 fe410523 ff114203 fe4102a3 fed14203 fe410223 fe412203 470233 24203 fe4104a3
  //   ff014203 fe4102a3 fec14203 fe410223 fe412203 470233 24203 fe410423 fe812703 c52603 fee12823 fe812e23
  //   3437 80840413 ff014183 3401b3 1c183 ff114203 440233 24203 4181b3 ff214203 440233 24203 4181b3
  //   ff314203 440233 24203 4181b3 3237 80020213 320233 24203 ffc12403 420233 420233 410233 66800193
  //   fe312823 28800193 fe312623 fec22203 20067 c68733 10000513 fe812e23 fe912c23 fee12823 50413 ff012483
  //   fe812423 feb14183 3181b3 fe312423 fe914183 3181b3 fe912423 feb14203 420233 fe412423 fe914203 4181b3
  //   3181b3 fe312a23 fe912423 33237 90020213 feb14183 4181b3 1c183 fe3103a3 fea14183 4181b3 1c183
  //   fe310323 fe914183 4181b3 1c183 fe3102a3 fe814183 4181b3 1c183 fe310223 ff412183 fe412203 440233
  //   120213 fe412423 feb14203 420233 fe412423 fe914203 4181b3 3237 90820213 320233 ff812483 ffc12403
  //   24203 420233 420233 410233 11b7 86818193 fe312823 39000193 fe312623 fec22203 20067 812703 10000513
  //   e78733 fe812e23 fe912c23 fee12823 50413 ff012483 fe812423 feb14183 3181b3 fe312423 fe914183 3181b3
  //   fe912423 feb14203 420233 fe412423 fe914203 4181b3 3181b3 fe312a23 fe912423 33237 90020213 feb14183
  //   4181b3 1c183 fe3103a3 fea14183 4181b3 1c183 fe310323 fe914183 4181b3 1c183 fe3102a3 fe814183 4181b3
  //   1c183 fe310223 ff412183 fe412203 440233 120213 fe412423 feb14203 420233 fe412423 fe914203 4181b3
  //   3237 90820213 320233 ff812483 ffc12403 24203 420233 420233 410233 11b7 86818193 fe312823 49c00193
  //   fe312623 fec22203 20067 8*f787b3 d787b3 f787b3 f787b3 20000437 f40433 812783 c60633 c60633 fef12423
  //   feb14183 3181b3 fe312423 fe914183 fff78213 fe412423 feb14203 420233 fe412423 fe914203 4181b3 3237
  //   91820213 418233 24203 420233 420233 410233 65400193 fe312823 54000193 fe312623 fec22203 20067 493
  //   40513 b12223 c12023 10b7 de008093 80e7 12603 412583 812783 148493 40040413 c585b3 fef12823 fe912623
  //   fe812e23 fe912c23 2437 70040413 ff014183 340233 100193 320023 fec14183 3401b3 18023 24183 ff114483
  //   940233 100493 920023 fed14483 9404b3 48023 24483 9181b3 ff214483 940233 100493 920023 fee14483
  //   9404b3 48023 24483 9181b3 ff314483 940233 100493 920023 fef14483 9404b3 48023 24483 9181b3 3237
  //   80020213 320233 24203 ff812483 ffc12403 420233 420233 410233 65400193 fe312823 54400193 fe312623
  //   fec22203 20067 1412083 1012403 c12483 1810113 8067 10000713 fec12823 fee12623 fe812e23 fe912c23 2437
  //   70040413 ff014183 340233 100193 320023 fec14183 3401b3 18023 24183 ff114483 940233 100493 920023
  //   fed14483 9404b3 48023 24483 9181b3 ff214483 940233 100493 920023 fee14483 9404b3 48023 24483 9181b3
  //   ff314483 940233 100493 920023 fef14483 9404b3 48023 24483 9181b3 3237 80020213 320233 24203 ff812483
  //   ffc12403 420233 420233 410233 74c00193 fe312823 28800193 fe312623 fec22203 20067 812703 fee12823
  //   fec12623 fe812e23 fe912c23 2437 70040413 ff014183 340233 100193 320023 fec14183 3401b3 18023 24183
  //   ff114483 940233 100493 920023 fed14483 9404b3 48023 24483 9181b3 ff214483 940233 100493 920023
  //   fee14483 9404b3 48023 24483 9181b3 ff314483 940233 100493 920023 fef14483 9404b3 48023 24483 9181b3
  //   3237 80020213 320233 24203 ff812483 ffc12403 420233 420233 410233 11b7 83418193 fe312823 39000193
  //   fe312623 fec22203 20067 1012403 1412083 c12483 40637 20000537 1810113 1237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
endmodule

module PC (
  input  [31:0] PC_load_data,
  input  PC_load_en,
  input  clk,
  input  PC_reset,
  output [31:0] PC_out_data
);

  wire [31:0] adder_1_out, multiplexer_1_out;

  Multiplexer #(.width(32)) multiplexer_1 (
    .in0(adder_1_out), .in1(PC_load_data), .out(multiplexer_1_out), .sel(PC_load_en));
  Register #(.width(32)) register_1 (.D(multiplexer_1_out), .en(1'b1), .clk(clk), .Q(PC_out_data), .clr(PC_reset));
  Adder #(.width(32)) adder_1 (.a(32'h4), .b(PC_out_data), .out(adder_1_out));  // open: cin, cout
endmodule

module load_word (
  input  [11:0] imm_11_0,
  input  [31:0] rdata1,
  input  lw_EN,
  input  [31:0] RAM_data_out,
  output [31:0] RAM_byte_addr_32,
  output RAM_OE,
  output [31:0] GPR_wdata
);

  wire [31:0] adder_1_out;
  wire [31:31] multiplexer_1_out;

  Multiplexer multiplexer_1 (.in0(1'b0), .in1(1'b1), .out(multiplexer_1_out[31]), .sel(imm_11_0[11]));
  Adder #(.width(32)) adder_1 (
    .a({{20{multiplexer_1_out[31]}}, imm_11_0}), .b(rdata1), .out(adder_1_out));  // open: cin, cout
  Multiplexer #(.width(32)) multiplexer_2 (.in0({32{1'b0}}), .in1(RAM_data_out), .out(GPR_wdata), .sel(lw_EN));
  Multiplexer #(.width(32)) multiplexer_3 (.in0({32{1'b0}}), .in1(adder_1_out), .out(RAM_byte_addr_32), .sel(lw_EN));

  assign RAM_OE = lw_EN;

  // Notes on the sheet:
  //   从地址中读取值存储到rd
  //   符号扩展立即数得到偏移量，与rs1内容相加得到地址
endmodule

module store_word (
  input  [4:0] imm_4_0,
  input  [6:0] imm_11_5,
  input  [31:0] rdata1,
  input  sw_EN,
  input  [31:0] rdata2,
  output [31:0] RAM_byte_addr_32,
  output RAM_WE,
  output [31:0] RAM_data_in
);

  wire [31:0] adder_1_out;
  wire [31:31] imm_sign_11_0;

  Multiplexer multiplexer_1 (.in0(1'b0), .in1(1'b1), .out(imm_sign_11_0[31]), .sel(imm_11_5[6]));
  Adder #(.width(32)) adder_1 (
    .a({{20{imm_sign_11_0[31]}}, imm_11_5, imm_4_0}), .b(rdata1), .out(adder_1_out));  // open: cin, cout
  Multiplexer #(.width(32)) multiplexer_2 (.in0({32{1'b0}}), .in1(rdata2), .out(RAM_data_in), .sel(sw_EN));
  Multiplexer #(.width(32)) multiplexer_3 (.in0({32{1'b0}}), .in1(adder_1_out), .out(RAM_byte_addr_32), .sel(sw_EN));

  assign RAM_WE = sw_EN;

  // Other names for the same wires on the sheet: imm_sign_11_0[30:0] = {{19{imm_sign_11_0[31]}}, imm_11_5, imm_4_0}

  // Notes on the sheet:
  //   采用S格式编码规范
  //   先把立即数符号扩展到32位，与rs1内容相加得到写入地址
  //   从rs2取到数据，启动RAM使能，并存储
endmodule

module add_immediate (
  input  [31:0] rdata1,
  input  [11:0] imm_11_0,
  input  addi_en,
  output [31:0] addi_result
);

  wire [31:0] adder_1_out;
  wire [31:31] multiplexer_1_out;

  Multiplexer multiplexer_1 (.in0(1'b0), .in1(1'b1), .out(multiplexer_1_out[31]), .sel(imm_11_0[11]));
  Adder #(.width(32)) adder_1 (
    .a({{20{multiplexer_1_out[31]}}, imm_11_0}), .b(rdata1), .out(adder_1_out));  // open: cin, cout
  Multiplexer #(.width(32)) multiplexer_2 (.in0({32{1'b0}}), .in1(adder_1_out), .out(addi_result), .sel(addi_en));

  // Notes on the sheet:
  //   I类型指令: imm[11:0] rs1 funct3 rd opcode
  //   ADDI指令将12位立即数进行符号扩展后与寄存器rs1的值相加，结果存入[rd]。算术溢出被忽略，运算结果仅保留结果的低XLEN位。
endmodule

module jump_and_link_register (
  input  [31:0] rdata1,
  input  [11:0] imm_11_0,
  input  jalr,
  output [31:0] jalr_target_addr
);

  wire [0:0] adder_1_out;
  wire [31:1] adder_1_out_2;
  wire [31:31] multiplexer_1_out;

  Multiplexer multiplexer_1 (.in0(1'b0), .in1(1'b1), .out(multiplexer_1_out[31]), .sel(imm_11_0[11]));
  Adder #(.width(32)) adder_1 (
    .a({{20{multiplexer_1_out[31]}}, imm_11_0}), .b(rdata1), .out({adder_1_out_2, adder_1_out[0]}));  // open: cin, cout
  Multiplexer #(.width(32)) multiplexer_2 (
    .in0({32{1'b0}}), .in1({adder_1_out_2, 1'b0}), .out(jalr_target_addr), .sel(jalr));

  // Notes on the sheet:
  //   I类型指令：
  //   立即数符号扩展+[rs1]->PC
  //   PC+4->[rd]
  //   imm[11:0] rs1 funct3 rd opcode
endmodule

module load_upper_immediate (
  input  [19:0] imm_31_12,
  input  lui_en,
  output [31:0] imm_lui
);

  Multiplexer #(.width(32)) multiplexer_1 (
    .in0({32{1'b0}}), .in1({imm_31_12, {12{1'b0}}}), .out(imm_lui), .sel(lui_en));

  // Notes on the sheet:
  //   U类型指令：低12位填0，高20位imm，结果存入[rd]
endmodule

module addd (
  input  [31:0] rdata1,
  input  [31:0] rdata2,
  input  addd_en,
  output [31:0] add_result
);

  wire [31:0] adder_1_out;

  Adder #(.width(32)) adder_1 (.a(rdata1), .b(rdata2), .out(adder_1_out));  // open: cin, cout
  Multiplexer #(.width(32)) multiplexer_1 (.in0({32{1'b0}}), .in1(adder_1_out), .out(add_result), .sel(addd_en));

  // Notes on the sheet:
  //   R类型指令，将rs1 rs2相加，结果放入rd
endmodule

module load_byte_unsigned (
  input  [11:0] imm_11_0,
  input  [31:0] rdata1,
  input  lbu_EN,
  input  [7:0] RAM_data_out,
  output [31:0] RAM_byte_addr_32,
  output RAM_OE,
  output [31:0] GPR_wdata
);

  wire [31:0] adder_1_out;
  wire [31:31] multiplexer_1_out;

  Multiplexer multiplexer_1 (.in0(1'b0), .in1(1'b1), .out(multiplexer_1_out[31]), .sel(imm_11_0[11]));
  Adder #(.width(32)) adder_1 (
    .a({{20{multiplexer_1_out[31]}}, imm_11_0}), .b(rdata1), .out(adder_1_out));  // open: cin, cout
  Multiplexer #(.width(32)) multiplexer_2 (.in0({32{1'b0}}), .in1(adder_1_out), .out(RAM_byte_addr_32), .sel(lbu_EN));
  Multiplexer #(.width(32)) multiplexer_3 (
    .in0({32{1'b0}}), .in1({{24{1'b0}}, RAM_data_out}), .out(GPR_wdata), .sel(lbu_EN));

  assign RAM_OE = lbu_EN;

  // Notes on the sheet:
  //   从地址读取8bit，零扩展到32bit，然后存入rd
endmodule

module store_byte (
  input  [4:0] imm_4_0,
  input  [6:0] imm_11_5,
  input  [31:0] rdata1,
  input  sb_EN,
  input  [31:0] rdata2,
  output [31:0] RAM_byte_addr_32,
  output RAM_WE,
  output [31:0] RAM_data_in
);

  wire [31:0] adder_1_out;
  wire [31:31] imm_sign_11_0;

  Multiplexer multiplexer_1 (.in0(1'b0), .in1(1'b1), .out(imm_sign_11_0[31]), .sel(imm_11_5[6]));
  Adder #(.width(32)) adder_1 (
    .a({{20{imm_sign_11_0[31]}}, imm_11_5, imm_4_0}), .b(rdata1), .out(adder_1_out));  // open: cin, cout
  Multiplexer #(.width(32)) multiplexer_2 (.in0({32{1'b0}}), .in1(rdata2), .out(RAM_data_in), .sel(sb_EN));
  Multiplexer #(.width(32)) multiplexer_3 (.in0({32{1'b0}}), .in1(adder_1_out), .out(RAM_byte_addr_32), .sel(sb_EN));

  assign RAM_WE = sb_EN;

  // Other names for the same wires on the sheet: imm_sign_11_0[30:0] = {{19{imm_sign_11_0[31]}}, imm_11_5, imm_4_0}

  // Notes on the sheet:
  //   采用S格式编码规范
  //   先把立即数符号扩展到32位，与rs1内容相加得到写入地址
  //   从rs2取到数据，启动RAM使能，并存储
endmodule
