// Logisim project Full_Adder.circ as structural Verilog: 1 circuit, main circuit main
module main (
  input  C_in,
  input  A,
  input  B,
  output S,
  output C_out
);

  wire and_1_out, and_2_out, and_3_out;

  and and_1 (and_1_out, A, B);
  and and_2 (and_2_out, B, C_in);
  and and_3 (and_3_out, A, C_in);
  ExactlyOne xor_1 (.out(S), .in0(C_in), .in1(A), .in2(B));
  or or_1 (C_out, and_1_out, and_2_out, and_3_out);
endmodule
