// Logisim project Multiplexer_4.circ as structural Verilog: 1 circuit, main circuit main
module main (
  input  [2:0] D0,
  input  [2:0] D1,
  input  [2:0] D2,
  input  [2:0] D3,
  input  [1:0] in_5,
  input  in_6,
  output [2:0] out_7
);

  wire and_1_out, and_2_out, and_3_out, and_4_out, decoder_1_out0, decoder_1_out1, decoder_1_out2,
       decoder_1_out3;

  Decoder #(.select(2)) decoder_1 (
    .out0(decoder_1_out0), .out1(decoder_1_out1), .out2(decoder_1_out2), .out3(decoder_1_out3), .sel(in_5),
    .en(in_6));
  and and_1 (and_1_out, D0[0], decoder_1_out0);
  and and_2 (and_2_out, D1[0], decoder_1_out1);
  and and_3 (and_3_out, D2[0], decoder_1_out2);
  and and_4 (and_4_out, decoder_1_out3, D3[0]);
  or or_1 (out_7[0], and_1_out, and_2_out, and_3_out, and_4_out);
  Multiplexer #(.select(2)) multiplexer_1 (
    .in0(D0[1]), .in1(D1[1]), .in2(D2[1]), .in3(D3[1]), .out(out_7[1]), .sel(in_5));
  Multiplexer #(.select(2)) multiplexer_2 (
    .in0(D0[2]), .in1(D1[2]), .in2(D2[2]), .in3(D3[2]), .out(out_7[2]), .sel(in_5));
endmodule
