// Logisim project Priority_Encoder.circ as structural Verilog
module PriorityEncoder_4To2 (
  input  A0,
  input  A1,
  input  A2,
  input  A3,
  output Y0,
  output Y1
);

  wire and_1_out, and_2_out, not_1_out, not_2_out;

  not not_1 (not_1_out, A3);
  not not_2 (not_2_out, A2);
  and and_1 (and_1_out, not_2_out, not_1_out, A1);
  and and_2 (and_2_out, A2, not_1_out);
  or or_1 (Y0, and_1_out, A3);
  or or_2 (Y1, and_2_out, A3);
endmodule
