// Logisim project RAM_register.circ as structural Verilog: 1 circuit, main circuit RAM_register
module RAM_register (
  input  [7:0] D,
  input  wen,
  input  [1:0] waddr,
  input  clk,
  input  [1:0] raddr1,
  input  [1:0] raddr2,
  output [7:0] Q,
  output [7:0] rdata1,
  output [7:0] rdata2
);

  wire and_1_out, and_2_out, and_3_out, and_4_out, decoder_1_out0, decoder_1_out1, decoder_1_out2,
       decoder_1_out3;
  wire [7:0] register_1_q, register_2_q, register_3_q, register_4_q;

  Decoder #(.select(2)) decoder_1 (
    .out0(decoder_1_out0), .out1(decoder_1_out1), .out2(decoder_1_out2), .out3(decoder_1_out3), .sel(waddr),
    .en(1'b1));
  and and_1 (and_1_out, decoder_1_out0, wen);
  and and_2 (and_2_out, decoder_1_out1, wen);
  and and_3 (and_3_out, decoder_1_out2, wen);
  and and_4 (and_4_out, decoder_1_out3, wen);
  Register register_1 (.D(D), .en(and_1_out), .clk(clk), .Q(register_1_q));  // open: clr
  Register register_2 (.D(D), .en(and_2_out), .clk(clk), .Q(register_2_q));  // open: clr
  Register register_3 (.D(D), .en(and_3_out), .clk(clk), .Q(register_3_q));  // open: clr
  Register register_4 (.D(D), .en(and_4_out), .clk(clk), .Q(register_4_q));  // open: clr
  Multiplexer #(.select(2), .width(8)) multiplexer_1 (
    .in0(register_1_q), .in1(register_2_q), .in2(register_3_q), .in3(register_4_q), .out(Q), .sel(waddr));
  Multiplexer #(.select(2), .width(8)) multiplexer_2 (
    .in0(register_1_q), .in1(register_2_q), .in2(register_3_q), .in3(register_4_q), .out(rdata1), .sel(raddr1));
  Multiplexer #(.select(2), .width(8)) multiplexer_3 (
    .in0(register_1_q), .in1(register_2_q), .in2(register_3_q), .in3(register_4_q), .out(rdata2), .sel(raddr2));
  // Probe on Q

  // Notes on the sheet:
  //   4(地址单元)*8(存储位)RAM
endmodule
