// Logisim project RBS.circ as structural Verilog: 1 circuit, main circuit main
module main (
  input  A0,
  input  B0,
  input  A1,
  input  B1,
  input  in_5,
  input  A2,
  input  B2,
  input  A3,
  input  B3,
  input  in_10,
  input  in_11
);

  wire ssgement_1_a, ssgement_1_b, ssgement_1_c, ssgement_1_d, ssgement_1_e, ssgement_1_f, ssgement_1_g,
       ssgement_2_a, ssgement_2_b, ssgement_2_c, ssgement_2_d, ssgement_2_e, ssgement_2_f, ssgement_2_g,
       ssgement_3_a, ssgement_3_b, ssgement_3_c, ssgement_3_d, ssgement_3_e, ssgement_3_f, ssgement_3_g,
       subtractor_1_bout, subtractor_1_out, subtractor_2_bout, subtractor_2_out, subtractor_3_bout,
       subtractor_3_out, subtractor_4_bout, subtractor_4_out;

  Subtractor #(.width(1)) subtractor_1 (.a(A0), .b(B0), .out(subtractor_1_out), .bout(subtractor_1_bout));  // open: bin
  Subtractor #(.width(1)) subtractor_2 (
    .a(A1), .b(B1), .out(subtractor_2_out), .bin(subtractor_1_bout), .bout(subtractor_2_bout));
  Subtractor #(.width(1)) subtractor_3 (
    .a(A2), .b(B2), .out(subtractor_3_out), .bin(subtractor_2_bout), .bout(subtractor_3_bout));
  Subtractor #(.width(1)) subtractor_4 (
    .a(A3), .b(B3), .out(subtractor_4_out), .bin(subtractor_3_bout), .bout(subtractor_4_bout));
  LED led_1 (.in(subtractor_4_bout));
  ssgement ssgement_1 (
    .in_1(A0), .in_2(A1), .in_3(A2), .in_4(A3), .in_5(in_10), .A(ssgement_1_a), .B(ssgement_1_b),
    .C(ssgement_1_c), .D(ssgement_1_d), .E(ssgement_1_e), .F(ssgement_1_f), .G(ssgement_1_g));
  ssgement ssgement_2 (
    .in_1(B0), .in_2(B1), .in_3(B2), .in_4(B3), .in_5(in_11), .A(ssgement_2_a), .B(ssgement_2_b),
    .C(ssgement_2_c), .D(ssgement_2_d), .E(ssgement_2_e), .F(ssgement_2_f), .G(ssgement_2_g));
  _7_Segment_Display u_7_segment_display_1 (
    .g(ssgement_1_g), .f(ssgement_1_f), .a(ssgement_1_a), .b(ssgement_1_b), .e(ssgement_1_e),
    .d(ssgement_1_d), .c(ssgement_1_c));  // open: dp
  ssgement ssgement_3 (
    .in_1(subtractor_1_out), .in_2(subtractor_2_out), .in_3(subtractor_3_out), .in_4(subtractor_4_out),
    .in_5(in_5), .A(ssgement_3_a), .B(ssgement_3_b), .C(ssgement_3_c), .D(ssgement_3_d), .E(ssgement_3_e),
    .F(ssgement_3_f), .G(ssgement_3_g));
  _7_Segment_Display u_7_segment_display_2 (
    .g(ssgement_2_g), .f(ssgement_2_f), .a(ssgement_2_a), .b(ssgement_2_b), .e(ssgement_2_e),
    .d(ssgement_2_d), .c(ssgement_2_c));  // open: dp
  _7_Segment_Display u_7_segment_display_3 (
    .g(ssgement_3_g), .f(ssgement_3_f), .a(ssgement_3_a), .b(ssgement_3_b), .e(ssgement_3_e),
    .d(ssgement_3_d), .c(ssgement_3_c));  // open: dp

  // Notes on the sheet:
  //   testcases:
  //   0011-0011=0000
  //   0000-0001=1111(借位)
  //   0000-0000=0000
  //   Ripple Borrow Subtractor：
endmodule
