// Logisim project ROM_mux.circ as structural Verilog: 1 circuit, main circuit ROM_mux
module ROM_mux (
  input  [2:0] Addr,
  output [7:0] out_2
);

  Multiplexer #(.select(3)) multiplexer_1 (
    .in0(1'b1), .in1(1'b1), .in2(1'b1), .in3(1'b1), .in4(1'b0), .in5(1'b0), .in6(1'b1), .in7(1'b1),
    .out(out_2[7]), .sel(Addr));
  Multiplexer #(.select(3)) multiplexer_2 (
    .in0(1'b0), .in1(1'b0), .in2(1'b0), .in3(1'b0), .in4(1'b0), .in5(1'b0), .in6(1'b1), .in7(1'b1),
    .out(out_2[6]), .sel(Addr));
  Multiplexer #(.select(3)) multiplexer_3 (
    .in0(1'b0), .in1(1'b0), .in2(1'b1), .in3(1'b1), .in4(1'b0), .in5(1'b1), .in6(1'b0), .in7(1'b0),
    .out(out_2[5]), .sel(Addr));
  Multiplexer #(.select(3)) multiplexer_4 (
    .in0(1'b0), .in1(1'b1), .in2(1'b0), .in3(1'b1), .in4(1'b1), .in5(1'b0), .in6(1'b1), .in7(1'b1),
    .out(out_2[4]), .sel(Addr));
  Multiplexer #(.select(3)) multiplexer_5 (
    .in0(1'b1), .in1(1'b0), .in2(1'b0), .in3(1'b0), .in4(1'b0), .in5(1'b1), .in6(1'b0), .in7(1'b1),
    .out(out_2[3]), .sel(Addr));
  Multiplexer #(.select(3)) multiplexer_6 (
    .in0(1'b0), .in1(1'b0), .in2(1'b0), .in3(1'b0), .in4(1'b1), .in5(1'b0), .in6(1'b0), .in7(1'b1),
    .out(out_2[2]), .sel(Addr));
  Multiplexer #(.select(3)) multiplexer_7 (
    .in0(1'b1), .in1(1'b0), .in2(1'b0), .in3(1'b0), .in4(1'b1), .in5(1'b0), .in6(1'b0), .in7(1'b1),
    .out(out_2[1]), .sel(Addr));
  Multiplexer #(.select(3)) multiplexer_8 (
    .in0(1'b0), .in1(1'b0), .in2(1'b0), .in3(1'b1), .in4(1'b1), .in5(1'b1), .in6(1'b1), .in7(1'b1),
    .out(out_2[0]), .sel(Addr));

  // Notes on the sheet:
  //   ROM->数列求和程序
  //   10001010  # 0: li r0, 10
  //   10010000  # 1: li r1, 0
  //   10100000  # 2: li r2, 0  
  //   10110001  # 3: li r3, 1
  //   00010111  # 4: add r1, r1, r3
  //   00101001  # 5: add r2, r2, r1
  //   11010001  # 6: bner0 r1, 4
  //   11011111  # 7: bner0 r3, 7 
endmodule
