// Logisim project S_R_latch.circ as structural Verilog: 1 circuit, main circuit main
module main (
);

  wire and_1_out, and_2_out, and_3_out, and_4_out, dipswitch_1_p1, dipswitch_1_p2, dipswitch_2_p1,
       dipswitch_2_p2, nor_1_out, nor_2_out;

  // DipSwitch #(.number(2)) dipswitch_1: pin names not known; wires that end beside it: dipswitch_1_p1, dipswitch_1_p2
  // DipSwitch #(.number(2)) dipswitch_2: pin names not known; wires that end beside it: dipswitch_2_p1, dipswitch_2_p2
  and and_1 (and_1_out, dipswitch_1_p1, dipswitch_1_p2);
  and and_2 (and_2_out, dipswitch_2_p1, dipswitch_2_p2);
  and and_3 (and_3_out, and_1_out, and_2_out);
  and and_4 (and_4_out, and_1_out, and_2_out);
  nor nor_1 (nor_1_out, and_3_out, nor_2_out);
  nor nor_2 (nor_2_out, nor_1_out, and_4_out);

  // Notes on the sheet:
  //   R
  //   S
  //   Q
  //   ~Q
endmodule
