// Logisim project Seven-segment digital tube decoder.circ as structural Verilog: 4 circuits, main circuit Seven_segment
module Decoder_2To4 (
  input  A0,
  input  A1,
  input  EN,
  output D0,
  output D1,
  output D2,
  output D3
);

  wire not_1_out, not_2_out;

  not not_1 (not_1_out, A0);
  not not_2 (not_2_out, A1);
  and and_1 (D0, not_1_out, EN, not_2_out);
  and and_2 (D1, not_1_out, EN, A1);
  and and_3 (D2, A0, EN, not_2_out);
  and and_4 (D3, A0, EN, A1);

  // Notes on the sheet:
  //   2-4译码器
endmodule

module Decoder_3To8 (
  input  A0,
  input  A1,
  input  A2,
  input  EN,
  output D0,
  output D1,
  output D2,
  output D3,
  output D4,
  output D5,
  output D6,
  output D7
);

  wire and_1_out, and_2_out, not_1_out;

  not not_1 (not_1_out, A2);
  and and_1 (and_1_out, not_1_out, EN);
  and and_2 (and_2_out, EN, A2);
  Decoder_2To4 decoder_2to4_1 (.A0(A0), .A1(A1), .EN(and_1_out), .D0(D0), .D1(D2), .D2(D4), .D3(D6));
  Decoder_2To4 decoder_2to4_2 (.A0(A0), .A1(A1), .EN(and_2_out), .D0(D1), .D1(D3), .D2(D5), .D3(D7));
endmodule

module Decoder_4To16 (
  input  A0,
  input  A1,
  input  A2,
  input  A3,
  input  EN,
  output D0,
  output D1,
  output D2,
  output D3,
  output D4,
  output D5,
  output D6,
  output D7,
  output D8,
  output D9,
  output D10,
  output D11,
  output D12,
  output D13,
  output D14,
  output D15
);

  wire and_1_out, and_2_out, not_1_out;

  not not_1 (not_1_out, A3);
  and and_1 (and_1_out, not_1_out, EN);
  and and_2 (and_2_out, EN, A3);
  Decoder_3To8 decoder_3to8_1 (
    .A0(A0), .A1(A1), .A2(A2), .EN(and_1_out), .D0(D0), .D1(D2), .D2(D4), .D3(D6), .D4(D8), .D5(D10),
    .D6(D12), .D7(D14));
  Decoder_3To8 decoder_3to8_2 (
    .A0(A0), .A1(A1), .A2(A2), .EN(and_2_out), .D0(D1), .D1(D3), .D2(D5), .D3(D7), .D4(D9), .D5(D11),
    .D6(D13), .D7(D15));
endmodule

module Seven_segment (
  input  in_1,
  input  in_2,
  input  in_3,
  input  in_4,
  input  in_5
);

  wire decoder_4to16_1_d0, decoder_4to16_1_d1, decoder_4to16_1_d2, decoder_4to16_1_d3, decoder_4to16_1_d4,
       decoder_4to16_1_d5, decoder_4to16_1_d6, decoder_4to16_1_d7, decoder_4to16_1_d8, decoder_4to16_1_d9,
       decoder_4to16_1_d10, decoder_4to16_1_d11, decoder_4to16_1_d12, decoder_4to16_1_d13,
       decoder_4to16_1_d14, decoder_4to16_1_d15, or_1_out, or_2_out, or_3_out, or_4_out, or_5_out, or_6_out,
       or_7_out, or_8_out;

  Decoder_4To16 decoder_4to16_1 (
    .A0(in_1), .A1(in_2), .A2(in_3), .A3(in_4), .EN(in_5), .D0(decoder_4to16_1_d0), .D1(decoder_4to16_1_d1),
    .D2(decoder_4to16_1_d2), .D3(decoder_4to16_1_d3), .D4(decoder_4to16_1_d4), .D5(decoder_4to16_1_d5),
    .D6(decoder_4to16_1_d6), .D7(decoder_4to16_1_d7), .D8(decoder_4to16_1_d8), .D9(decoder_4to16_1_d9),
    .D10(decoder_4to16_1_d10), .D11(decoder_4to16_1_d11), .D12(decoder_4to16_1_d12),
    .D13(decoder_4to16_1_d13), .D14(decoder_4to16_1_d14), .D15(decoder_4to16_1_d15));
  or or_1 (or_1_out, decoder_4to16_1_d0, decoder_4to16_1_d2, decoder_4to16_1_d3, decoder_4to16_1_d5, decoder_4to16_1_d6, decoder_4to16_1_d7, decoder_4to16_1_d8, decoder_4to16_1_d9);
  or or_2 (or_2_out, decoder_4to16_1_d0, decoder_4to16_1_d1, decoder_4to16_1_d2, decoder_4to16_1_d3, decoder_4to16_1_d7, decoder_4to16_1_d8, decoder_4to16_1_d4, decoder_4to16_1_d9);
  or or_3 (or_3_out, decoder_4to16_1_d0, decoder_4to16_1_d1, decoder_4to16_1_d3, decoder_4to16_1_d4, decoder_4to16_1_d5, decoder_4to16_1_d6, decoder_4to16_1_d7, decoder_4to16_1_d8, decoder_4to16_1_d9);
  or or_4 (or_4_out, decoder_4to16_1_d0, decoder_4to16_1_d2, decoder_4to16_1_d3, decoder_4to16_1_d5, decoder_4to16_1_d6, decoder_4to16_1_d8, decoder_4to16_1_d9);
  _7_Segment_Display u_7_segment_display_1 (
    .g(or_7_out), .f(or_6_out), .a(or_1_out), .b(or_2_out), .e(or_5_out), .d(or_4_out), .c(or_3_out),
    .dp(or_8_out));
  or or_5 (or_5_out, decoder_4to16_1_d0, decoder_4to16_1_d2, decoder_4to16_1_d6, decoder_4to16_1_d8);
  or or_6 (or_6_out, decoder_4to16_1_d0, decoder_4to16_1_d4, decoder_4to16_1_d5, decoder_4to16_1_d6, decoder_4to16_1_d8, decoder_4to16_1_d9);
  or or_7 (or_7_out, decoder_4to16_1_d2, decoder_4to16_1_d3, decoder_4to16_1_d4, decoder_4to16_1_d5, decoder_4to16_1_d6, decoder_4to16_1_d8, decoder_4to16_1_d9);
  or or_8 (or_8_out, decoder_4to16_1_d10, decoder_4to16_1_d11, decoder_4to16_1_d12, decoder_4to16_1_d15, decoder_4to16_1_d13, decoder_4to16_1_d14);

  // Notes on the sheet:
  //   0=>ABCDEF
  //   1=>BC
  //   2=>ABGED
  //   3=>ABCDG
  //   6=>ACDEFG
  //   7=>ABC
  //   8=>ABCDEFG
  //   9=>ACDFG
endmodule
