// Logisim project Sign_Magnitude_Adder_4.circ as structural Verilog: 2 circuits, main circuit main
module main (
  input  A0,
  input  B0,
  input  in_3,
  input  A1,
  input  B1,
  input  A2,
  input  B2,
  input  A3,
  input  B3
);

  wire adder_1_cout, and_1_out, and_2_out, comparator_1_lt, multiplexer_2_out, not_1_out, ssgement_1_a,
       ssgement_1_b, ssgement_1_c, ssgement_1_d, ssgement_1_e, ssgement_1_f, ssgement_1_g;
  wire [2:0] adder_1_out, multiplexer_1_out, multiplexer_3_out, subtractor_1_out, subtractor_2_out;

  Comparator #(.mode("unsigned"), .width(3)) comparator_1 (
    .a({A2, A1, A0}), .b({B2, B1, B0}), .lt(comparator_1_lt));  // open: gt, eq
  Adder #(.width(3)) adder_1 (.a({A2, A1, A0}), .b({B2, B1, B0}), .out(adder_1_out), .cout(adder_1_cout));  // open: cin
  not not_1 (not_1_out, multiplexer_2_out);
  Subtractor #(.width(3)) subtractor_1 (.a({A2, A1, A0}), .b({B2, B1, B0}), .out(subtractor_1_out));  // open: bin, bout
  Subtractor #(.width(3)) subtractor_2 (.a({B2, B1, B0}), .b({A2, A1, A0}), .out(subtractor_2_out));  // open: bin, bout
  and and_1 (and_1_out, multiplexer_2_out, adder_1_cout);
  LED led_1 (.in(and_1_out));
  and and_2 (and_2_out, not_1_out, adder_1_cout);
  LED led_2 (.in(and_2_out));
  Multiplexer #(.width(3)) multiplexer_1 (
    .in0(subtractor_1_out), .in1(subtractor_2_out), .out(multiplexer_1_out), .sel(comparator_1_lt));
  Multiplexer multiplexer_2 (.in0(A3), .in1(B3), .out(multiplexer_2_out), .sel(comparator_1_lt));
  Multiplexer #(.select(2), .width(3)) multiplexer_3 (
    .in0(adder_1_out), .in1(multiplexer_1_out), .in2(multiplexer_1_out), .in3(adder_1_out),
    .out(multiplexer_3_out), .sel({B3, A3}));
  _7_Segment_Display u_7_segment_display_1 (.g(multiplexer_2_out));  // open: f, a, b, e, d, c, dp
  _7_Segment_Display u_7_segment_display_2 (
    .g(ssgement_1_g), .f(ssgement_1_f), .a(ssgement_1_a), .b(ssgement_1_b), .e(ssgement_1_e),
    .d(ssgement_1_d), .c(ssgement_1_c));  // open: dp
  ssgement ssgement_1 (
    .in_1(multiplexer_3_out[0]), .in_2(multiplexer_3_out[1]), .in_3(multiplexer_3_out[2]), .in_5(in_3),
    .A(ssgement_1_a), .B(ssgement_1_b), .C(ssgement_1_c), .D(ssgement_1_d), .E(ssgement_1_e),
    .F(ssgement_1_f), .G(ssgement_1_g));  // open: in_4

  // Notes on the sheet:
  //   RCA
  //   A的绝对值更大，符号随A
  //   B的绝对值更大，符号随B
  //   RBS
  //   A的符号
  //   正数溢出
  //   B的符号
  //   负数溢出
  //   Sign-Magnitude Adder: 
  //   testcases:
  //   0100+0101=0001(正溢出)
  //   1011+1010=1101(负数加)
  //   1100+1101=1001(负溢出)
  //   0101+1011=0010(异号,正大)
  //   1101+0010=1011(异号,负大)
  //   0011+1011=0000(相消得零)
  //   0111+0000=0111(边界值)
  //   0000+0000=0000
  //   1000+0011=0011(负零处理)
  //   0100+0101=1001(基础正相加)
endmodule

module Ones_Complement_Adder (
  input  A0,
  input  B0,
  input  in_3,
  input  A1,
  input  B1,
  input  A2,
  input  B2,
  input  A3,
  input  B3
);

  wire adder_1_cout, and_1_out, and_2_out, comparator_1_lt, multiplexer_8_out, not_1_out, not_2_out,
       not_3_out, not_4_out, not_5_out, not_6_out, not_7_out, ssgement_1_a, ssgement_1_b, ssgement_1_c,
       ssgement_1_d, ssgement_1_e, ssgement_1_f, ssgement_1_g;
  wire [2:0] adder_1_out, multiplexer_1_out, multiplexer_4_out, multiplexer_7_out, multiplexer_9_out,
       subtractor_1_out, subtractor_2_out;

  not not_1 (not_1_out, A0);
  not not_2 (not_2_out, B0);
  not not_3 (not_3_out, A1);
  not not_4 (not_4_out, B1);
  not not_5 (not_5_out, A2);
  not not_6 (not_6_out, B2);
  Multiplexer multiplexer_1 (.in0(A0), .in1(not_1_out), .out(multiplexer_1_out[0]), .sel(A3));
  Multiplexer multiplexer_2 (.in0(A1), .in1(not_3_out), .out(multiplexer_1_out[1]), .sel(A3));
  Multiplexer multiplexer_3 (.in0(A2), .in1(not_5_out), .out(multiplexer_1_out[2]), .sel(A3));
  Multiplexer multiplexer_4 (.in0(B0), .in1(not_2_out), .out(multiplexer_4_out[0]), .sel(B3));
  Multiplexer multiplexer_5 (.in0(B1), .in1(not_4_out), .out(multiplexer_4_out[1]), .sel(B3));
  Multiplexer multiplexer_6 (.in0(B2), .in1(not_6_out), .out(multiplexer_4_out[2]), .sel(B3));
  Adder #(.width(3)) adder_1 (
    .a(multiplexer_1_out), .b(multiplexer_4_out), .out(adder_1_out), .cout(adder_1_cout));  // open: cin
  Comparator #(.mode("unsigned"), .width(3)) comparator_1 (
    .a(multiplexer_1_out), .b(multiplexer_4_out), .lt(comparator_1_lt));  // open: gt, eq
  not not_7 (not_7_out, multiplexer_8_out);
  Subtractor #(.width(3)) subtractor_1 (
    .a(multiplexer_1_out), .b(multiplexer_4_out), .out(subtractor_1_out));  // open: bin, bout
  Subtractor #(.width(3)) subtractor_2 (
    .a(multiplexer_4_out), .b(multiplexer_1_out), .out(subtractor_2_out));  // open: bin, bout
  and and_1 (and_1_out, multiplexer_8_out, adder_1_cout);
  LED led_1 (.in(and_2_out));
  and and_2 (and_2_out, not_7_out, adder_1_cout);
  LED led_2 (.in(and_1_out));
  Multiplexer #(.width(3)) multiplexer_7 (
    .in0(subtractor_1_out), .in1(subtractor_2_out), .out(multiplexer_7_out), .sel(comparator_1_lt));
  Multiplexer multiplexer_8 (.in0(A3), .in1(B3), .out(multiplexer_8_out), .sel(comparator_1_lt));
  Multiplexer #(.select(2), .width(3)) multiplexer_9 (
    .in0(adder_1_out), .in1(multiplexer_7_out), .in2(multiplexer_7_out), .in3(adder_1_out),
    .out(multiplexer_9_out), .sel({B3, A3}));
  _7_Segment_Display u_7_segment_display_1 (.g(multiplexer_8_out));  // open: f, a, b, e, d, c, dp
  _7_Segment_Display u_7_segment_display_2 (
    .g(ssgement_1_g), .f(ssgement_1_f), .a(ssgement_1_a), .b(ssgement_1_b), .e(ssgement_1_e),
    .d(ssgement_1_d), .c(ssgement_1_c));  // open: dp
  ssgement ssgement_1 (
    .in_1(multiplexer_9_out[0]), .in_2(multiplexer_9_out[1]), .in_3(multiplexer_9_out[2]), .in_5(in_3),
    .A(ssgement_1_a), .B(ssgement_1_b), .C(ssgement_1_c), .D(ssgement_1_d), .E(ssgement_1_e),
    .F(ssgement_1_f), .G(ssgement_1_g));  // open: in_4

  // Notes on the sheet:
  //   B0
  //   A0
  //   A2
  //   A1
  //   B1
  //   方法一：如上在原码加法器的基础上对反码的情况将反码变成原码
  //   方法二：是在普通 RCA 基础上添加循环进位的反码加法器方案
  //   B2
  //   A的符号
  //   B的符号
  //   RCA
  //   A的绝对值更大，符号随A
  //   B的绝对值更大，符号随B
  //   RBS
  //   负数溢出
  //   正数溢出
endmodule
