// Logisim project Summaion_circuit.circ as structural Verilog: 1 circuit, main circuit main
module main (
  input  in_1,
  input  in_2,
  input  in_3,
  input  in_4
);

  wire clock_1_out, t_ff_1_q;
  wire [3:0] adder_1_out, register_1_q, register_2_q;
  wire [7:0] adder_2_out, register_3_q;

  Clock clock_1 (.out(clock_1_out));
  Register #(.width(4)) register_1 (.D(register_2_q), .en(in_1), .clk(clock_1_out), .Q(register_1_q), .clr(in_2));
  T_Flip_Flop t_ff_1 (.T(in_3), .clk(clock_1_out), .Q(t_ff_1_q));  // open: Qn, reset, preset
  Adder #(.width(4)) adder_1 (.a(register_1_q), .b(4'b0001), .out(adder_1_out));  // open: cin, cout
  Register #(.width(4)) register_2 (.D(adder_1_out), .en(in_1), .clk(clock_1_out), .Q(register_2_q), .clr(in_2));
  Register register_3 (.D(adder_2_out), .en(in_1), .clk(t_ff_1_q), .Q(register_3_q), .clr(in_2));
  Adder adder_2 (.a({{4{in_4}}, register_2_q}), .b(register_3_q), .out(adder_2_out));  // open: cin, cout
  Hex_Digit_Display hex_digit_display_1 (.value(register_3_q[7:4]));  // open: dp
  Hex_Digit_Display hex_digit_display_2 (.value(register_3_q[3:0]));  // open: dp

  // Notes on the sheet:
  //   数列求和电路(8位)
endmodule
