// Logisim project clock.circ as structural Verilog: 1 circuit, main circuit main
module main (
  input  in_1
);

  wire and_1_out, clock_1_out, comparator_1_eq, comparator_1_gt, comparator_2_gt;
  wire [3:0] adder_1_out, adder_2_out, register_1_q, register_2_q;

  Hex_Digit_Display hex_digit_display_1 ();  // open: value, dp
  Clock clock_1 (.out(clock_1_out));
  Hex_Digit_Display hex_digit_display_2 ();  // open: value, dp
  Hex_Digit_Display hex_digit_display_3 ();  // open: value, dp
  Hex_Digit_Display hex_digit_display_4 ();  // open: value, dp
  Register #(.width(4)) register_1 (
    .D(adder_1_out), .en(in_1), .clk(clock_1_out), .Q(register_1_q), .clr(comparator_1_gt));
  Hex_Digit_Display hex_digit_display_5 (.value(register_2_q));  // open: dp
  Hex_Digit_Display hex_digit_display_6 (.value(register_1_q));  // open: dp
  Adder #(.width(4)) adder_1 (.a(4'b0001), .b(register_1_q), .out(adder_1_out));  // open: cin, cout
  Comparator #(.mode("unsigned"), .width(4)) comparator_1 (
    .a(register_1_q), .b(4'b1001), .gt(comparator_1_gt), .eq(comparator_1_eq));  // open: lt
  Register #(.width(4)) register_2 (
    .D(adder_2_out), .en(comparator_1_eq), .clk(clock_1_out), .Q(register_2_q), .clr(and_1_out));
  Adder #(.width(4)) adder_2 (.a(4'b0001), .b(register_2_q), .out(adder_2_out));  // open: cin, cout
  Comparator #(.mode("unsigned"), .width(4)) comparator_2 (
    .a(register_2_q), .b(4'b0101), .gt(comparator_2_gt));  // open: eq, lt
  and and_1 (and_1_out, comparator_2_gt, comparator_1_gt);
endmodule
