// Logisim project counter_4.circ as structural Verilog: 1 circuit, main circuit main
module main (
  input  in_1,
  input  in_2,
  input  in_3
);

  wire adder_1_cout, clock_1_out, ssgement_1_a, ssgement_1_b, ssgement_1_c, ssgement_1_d, ssgement_1_e,
       ssgement_1_f, ssgement_1_g;
  wire [3:0] adder_1_out, register_1_q;

  Clock clock_1 (.out(clock_1_out));
  Register #(.width(4)) register_1 (.D(adder_1_out), .en(in_1), .clk(clock_1_out), .Q(register_1_q), .clr(in_2));
  Adder #(.width(4)) adder_1 (.a(register_1_q), .b(4'b0001), .out(adder_1_out), .cout(adder_1_cout));  // open: cin
  ssgement ssgement_1 (
    .in_1(adder_1_out[0]), .in_2(adder_1_out[1]), .in_3(adder_1_out[2]), .in_4(adder_1_out[3]), .in_5(in_3),
    .A(ssgement_1_a), .B(ssgement_1_b), .C(ssgement_1_c), .D(ssgement_1_d), .E(ssgement_1_e),
    .F(ssgement_1_f), .G(ssgement_1_g));
  _7_Segment_Display u_7_segment_display_1 (
    .g(ssgement_1_g), .f(ssgement_1_f), .a(ssgement_1_a), .b(ssgement_1_b), .e(ssgement_1_e),
    .d(ssgement_1_d), .c(ssgement_1_c));  // open: dp

  // Notes on the sheet:
  //   4位计数器
endmodule
