// Logisim project sCPU.circ as structural Verilog: 1 circuit, main circuit main
module main (
  input  in_1,
  input  in_2,
  input  in_3,
  input  in_4
);

  wire and_1_out, clock_1_out, clock_2_out, comparator_1_eq, comparator_1_gt, comparator_1_lt,
       decoder_1_out0, decoder_1_out1, decoder_1_out2, decoder_1_out3, or_1_out, or_2_out, undriven_2,
       undriven_3;
  wire [1:0] multiplexer_2_out;
  wire [3:0] ram_register_1_rdata1, ram_register_1_rdata1_2;
  wire [7:0] adder_1_out, counter_1_q, multiplexer_1_out, ram_register_1_q, ram_register_1_rdata2,
       rom_mux_1_out_2, undriven;

  Clock clock_1 (.out(clock_1_out));
  Counter #(.max('h7)) counter_1 (
    .clr(in_1), .load(and_1_out), .up(in_3), .count(in_4), .clk(clock_1_out),
    .D({4'b0000, rom_mux_1_out_2[5:2]}), .Q(counter_1_q));  // open: carry
  // Probe on counter_1_q[2:0]
  Clock clock_2 (.out(clock_2_out));
  Multiplexer #(.width(8)) multiplexer_1 (
    .in0(adder_1_out), .in1({{4{in_2}}, rom_mux_1_out_2[3:0]}), .out(multiplexer_1_out), .sel(decoder_1_out2));
  Decoder #(.select(2)) decoder_1 (
    .out0(decoder_1_out0), .out1(decoder_1_out1), .out2(decoder_1_out2), .out3(decoder_1_out3),
    .sel(rom_mux_1_out_2[7:6]), .en(in_4));
  or or_1 (or_1_out, decoder_1_out2, decoder_1_out0);
  // Probe on multiplexer_2_out
  // Probe on rom_mux_1_out_2[5:4]
  ROM_mux rom_mux_1 (.Addr(counter_1_q[2:0]), .out_2(rom_mux_1_out_2));
  RAM_register ram_register_1 (
    .D(multiplexer_1_out), .wen(or_1_out), .waddr(rom_mux_1_out_2[5:4]), .clk(clock_2_out),
    .raddr1(multiplexer_2_out), .raddr2(rom_mux_1_out_2[1:0]), .Q(ram_register_1_q),
    .rdata1({ram_register_1_rdata1_2, ram_register_1_rdata1}), .rdata2(ram_register_1_rdata2));
  Multiplexer #(.width(2)) multiplexer_2 (
    .in0(rom_mux_1_out_2[3:2]), .in1(2'b00), .out(multiplexer_2_out), .sel(decoder_1_out3));
  Comparator comparator_1 (
    .a(ram_register_1_rdata2), .b({ram_register_1_rdata1_2, ram_register_1_rdata1}), .gt(comparator_1_gt),
    .eq(comparator_1_eq), .lt(comparator_1_lt));
  Adder adder_1 (
    .a({ram_register_1_rdata1_2, ram_register_1_rdata1}), .b(ram_register_1_rdata2), .out(adder_1_out));  // open: cin, cout
  Multiplexer #(.width(4)) multiplexer_3 (
    .in0(undriven[3:0]), .in1(ram_register_1_rdata1), .sel(undriven_2));  // open: out
  or or_2 (or_2_out, comparator_1_gt, comparator_1_lt);
  // Probe on {ram_register_1_rdata1_2, ram_register_1_rdata1}
  Hex_Digit_Display hex_digit_display_1 ();  // open: value, dp
  Multiplexer #(.width(4)) multiplexer_4 (
    .in0(undriven[7:4]), .in1(ram_register_1_rdata1_2), .sel(undriven_3));  // open: out
  and and_1 (and_1_out, or_2_out, decoder_1_out3);
  // Probe on ram_register_1_rdata2

  // Notes on the sheet:
  //   rd
  //   rs1
  //   rs2
endmodule
